# Fritzing sketch fritziing_ChristmasLights (saved by Fritzing 0.9.6b)

parts:
  Arduino1 = Arduino Nano (Rev3.0)
  S1 = Pushbutton [package="[THT]"]
  NEOPIXEL1 = Neopixel Strip -- Black (30/m)

nets:
  GND: Arduino1.GND, S1.Pin_3, NEOPIXEL1.GND
  N1: Arduino1.D6, NEOPIXEL1.DI
  N2: Arduino1.D7, S1.Pin_1, S1.Pin_2
  VIN: Arduino1.VIN, NEOPIXEL1.+5V

custom parts:
  Neopixel Strip -- Black (30/m): Neopixel Strip, Black, 30 pixels per meter.
